# Fritzing sketch Untitled Sketch (saved by Fritzing 0.9.3b)
circuit board: 8.46667cm x 5.64444cm

parts:
  U1 = NodeMCU V1.0
  R1 = Resistor [tolerance=±5% resistance=220 package=THT]
  R2 = Resistor [tolerance=±5% resistance=220 package=THT]
  Danger_Red = LED - 5mm [color="Red (633nm)" package="5 mm [THT]"]
  Safe_Green = LED - 5mm [color="Green (555nm)" package="5 mm [THT]"]
  hc-sr2 = hc-sr04

nets:
  N1: U1.D1, hc-sr2.Trig
  N2: U1.D2, hc-sr2.Echo
  N3: U1.D3, R1.Pin_0
  N4: U1.D4, R2.Pin_0
  GND: U1.GND, Danger_Red.cathode, Safe_Green.cathode, hc-sr2.GND
  VIN: U1.Vin, hc-sr2.VCC
  N5: R1.Pin_1, Danger_Red.anode
  N6: R2.Pin_1, Safe_Green.anode

custom parts:
  NodeMCU V1.0: ESP8266 based NodeMCU
  hc-sr04: This is a HC-SR04 Distance Sensor

// code stored in the sketch: Untitled.ino

